# Fritzing sketch Exp09_LunchBox_HelloResetSource (saved by Fritzing 0.9.3b)
breadboards: 1

parts:
  Part1 = DIP - 18 pins
  SW3 = Pushbutton [package="[SMD]"]
  SW2 = Pushbutton [package="[SMD]"]
  SW1 = Pushbutton [package="[SMD]"]
  R3 = Resistor [tolerance=±5% resistance=1k package="1206 [SMD]"]
  R2 = Resistor [tolerance=±5% resistance=1k package="1206 [SMD]"]
  R1 = Resistor [tolerance=±5% resistance=1k package="1206 [SMD]"]

nets:
  N1: Part1.3V3, R3.Pin_0, R2.Pin_0, R1.Pin_0
  N2: Part1.P1.3, SW1.Pin_3, SW1.Pin_4, R1.Pin_1
  N3: Part1.P1.4, SW2.Pin_3, SW2.Pin_4, R2.Pin_1
  N4: Part1.P1.5, SW3.Pin_3, SW3.Pin_4, R3.Pin_1
  N5: Part1.GND, SW3.Pin_1, SW3.Pin_2, SW2.Pin_1, SW2.Pin_2, SW1.Pin_1, SW1.Pin_2
